# Fritzing sketch breadboard (saved by Fritzing 0.9.4)
breadboards: 1

parts:
  Part1 = node32s
  BMP280_Breakout1 = BMP280 Breakout Board [part_number=BMP280]
  R1 = Resistor [tolerance=±5% resistance=220 package=THT]
  R2 = Resistor [tolerance=±5% resistance=220 package=THT]
  LED2 = LED - 3mm [color="Red (633nm)" package="3 mm [THT]"]
  LED1 = LED - 3mm [color="Green (555nm)" package="3 mm [THT]"]

nets:
  3.3V: Part1.3.3V, BMP280_Breakout1.VCC
  N1: Part1.IO32, LED1.anode
  N2: Part1.IO33, LED2.anode
  N3: Part1.V_BATT, BMP280_Breakout1.GND, R1.Pin_1, R2.Pin_1
  N4: Part1.IO22, BMP280_Breakout1.SCL
  N5: Part1.IO21, BMP280_Breakout1.SDA
  N6: R1.Pin_0, LED1.cathode
  N7: R2.Pin_0, LED2.cathode

custom parts:
  BMP280 Breakout Board: This is a breakout board for the Bosch Sensortec BMP280, "an absolute barometric pressure sensor especially designed for mobile applications." The operation range is 300 to 1100 hPa. Supply voltage is 1.2 to 3.6V. Operating temperature range is -40 to +85 °C.
