# Fritzing sketch breadboard (saved by Fritzing 0.9.4)
breadboards: 1

parts:
  Part2 = node32s
  MQ-3_Sensor1 = MQ-3 Breakout Board

nets:
  N1: Part2.IO32, MQ-3_Sensor1.AOUT
  N2: Part2.IO33, MQ-3_Sensor1.GND
  N3: Part2.V_BATT, MQ-3_Sensor1.DOUT
  5V: Part2.5V, MQ-3_Sensor1.5V

custom parts:
  MQ-3 Breakout Board: MQ-3 alcohol gas sensor breakout board. Input voltage is 5V. Sensor output is available in analog and digital.
